# Fritzing sketch simple_neopixel (saved by Fritzing 0.9.3b)

parts:
  Composant1 = Arduino Uno (Rev3)
  R1 = Resistor [tolerance=±5% resistance=470 package=THT]
  Composant2 = ws2812b [package="smd 2812b"]

nets:
  N1: Composant1.D6_PWM, R1.Pin_0
  5V: Composant1.5V, Composant2.VDD
  GND: Composant1.GND, Composant2.VSS
  N2: R1.Pin_1, Composant2.DIN
